# Fritzing sketch Schematics (saved by Fritzing 0.9.3b)
breadboards: 1

parts:
  L1 = Solenoid
  Part1 = Arduino Mega 2560 (Rev3)
  U1 = POT [package=pot_mammoth]
  LCD1 = LCD screen
  Part2 = Soil Moisture Sensor
  Part3 = Bluetooth HC-05 Macho
  Q1 = NPN-Transistor [package="TO92 [THT]"]
  VCC1 = Battery block 9V
  DHT1 = DHT11 Humitidy and Temperature Sensor

nets:
  N1: L1.pin1, VCC1.-
  GND: L1.pin2, Part1.GND, LCD1.R/W, LCD1.LED-, Part2.GND, Part3.GND, Q1.E, DHT1.GND
  N2: Part1.A0, Part2.SIG
  N3: Part1.A1, DHT1.DATA
  N4: Part1.D0_RX0, Part3.TXD
  N5: Part1.D1_TX0, Part3.RXD
  VDD: Part1.5V, LCD1.VDD, LCD1.LED+, Part2.VCC, Part3.VCC, DHT1.VDD
  N6: Part1.D22, LCD1.DB7
  N7: Part1.D24, LCD1.DB6
  N8: Part1.D26, LCD1.DB5
  N9: Part1.D28, LCD1.DB4
  N10: Part1.D30, LCD1.E
  N11: Part1.D32, LCD1.RS
  N12: Part1.D34, Q1.B
  N13: U1.S, LCD1.VSS
  N14: U1.A, LCD1.V0
  N15: Q1.C, VCC1.+

custom parts:
  DHT11 Humitidy and Temperature Sensor: DHT11 Humidity and Temperature Sensor
